// Logisim project S2-T13.circ as structural Verilog: 1 circuit, main circuit main
module main (
  input  P1,
  input  P0,
  input  Switch,
  input  P1_prime,
  input  P0_prime,
  input  N1,
  input  N0,
  input  E1_prime,
  input  E0_prime,
  input  E1,
  input  E0,
  input  Enable,
  input  Enable_2,
  input  Enable_3,
  input  Enable_4,
  input  Clear,
  input  Clear_2,
  input  Clear_3,
  input  Clear_4,
  input  Max_Capacity,
  input  Max_Capacity_2,
  input  Max_Capacity_3,
  input  Max_Capacity_4,
  input  in_24,
  input  in_25,
  input  in_26,
  input  in_27,
  input  in_28,
  input  in_29,
  input  in_30,
  input  in_31,
  input  in_32,
  input  in_33,
  input  in_34,
  input  in_35,
  input  Alarm,
  input  Alarm_2,
  input  Alarm_3,
  input  Alarm_4,
  input  Enable_5,
  input  Enable_6,
  input  Enable_7,
  input  Enable_8
);

  wire A_out, and_1_out, and_2_out, and_3_out, and_4_out, and_5_out, and_6_out, and_7_out, Clock_2_out,
       Clock_3_out, Clock_4_out, Clock_out, Enter_2_out, Enter_3_out, Enter_4_out, Enter_out, ES1_o, ES2_o,
       ES3_o, ES4_o, main_1_stop, main_2_vi, main_3_pc_b0, main_3_pc_b1, main_3_pc_b2, main_3_pc_b3,
       main_4_stop, main_5_pc_b0, main_5_pc_b1, main_5_pc_b2, main_5_pc_b3, main_6_vi, main_7_stop,
       main_8_pc_b0, main_8_pc_b1, main_8_pc_b2, main_8_pc_b3, main_9_vi, main_10_stop, main_11_pc_b0,
       main_11_pc_b1, main_11_pc_b2, main_11_pc_b3, main_12_vi, nor_1_out, nor_2_out, not_1_out, not_2_out,
       not_3_out, not_4_out, not_5_out, not_6_out, not_7_out, not_8_out, not_9_out, not_10_out, not_11_out,
       not_12_out, or_1_out, or_2_out, or_3_out, or_4_out, or_5_out, or_6_out, or_7_out, or_8_out, s1_out,
       s2_out, s3_out, s4_out, START_2_out, START_3_out, START_4_out, START_out, xnor_1_out;
  wire [3:0] main_3_tc_b0, main_5_tc_b0, main_8_tc_b0, main_11_tc_b0;

  Button Enter (.out(Enter_out));
  Button START (.out(START_out));
  Clock Clock (.out(Clock_out));
  nor nor_1 (nor_1_out, ES1_o, ES2_o, ES3_o, ES4_o);
  or or_1 (or_1_out, Clear, Alarm);
  Time_Counter_main main_1 (.START(START_out), .Enable(Enable_5), .Clock(Clock_out), .STOP(main_1_stop));
  Event_Switcher_main ES1 (.K(Switch), .A(P1), .B(P1_prime), .O(ES1_o));
  Event_Switcher_main ES2 (.K(Switch), .A(P0), .B(P0_prime), .O(ES2_o));
  Event_Switcher_main ES3 (.K(Switch), .A(E1), .B(N1), .O(ES3_o));
  Event_Switcher_main ES4 (.K(Switch), .A(E0), .B(N0), .O(ES4_o));
  nor nor_2 (nor_2_out, ES4_o, ES3_o);
  xnor xnor_1 (xnor_1_out, ES2_o, ES1_o);
  Vacancy_Indicator_main main_2 (
    .P1(ES1_o), .P0(ES2_o), .A3(main_3_pc_b3), .A2(main_3_pc_b2), .A1(main_3_pc_b1), .A0(main_3_pc_b0),
    .M3(Max_Capacity), .M2(in_24), .M1(in_28), .M0(in_32), .VI(main_2_vi));  // open: Seat_Allotment__SA
  LED led_1 (.in(Alarm));
  not not_1 (not_1_out, ES2_o);
  and and_1 (and_1_out, nor_2_out, xnor_1_out);
  Seat_Allocator_main main_3 (
    .TC_Button(Enter_out), .TC_Enable(Enable), .TC_Clear(Clear), .PC_Button(Enter_out), .PC_Enable(Enable),
    .PC_Clear(or_1_out), .PC_A3(1'b0), .PC_S3(1'b0), .PC_A2(1'b0), .PC_S2(1'b0), .PC_A1(1'b0), .PC_S1(1'b0),
    .PC_Ci(1'b0), .Bi(1'b0), .SA_PC_A0(nor_1_out), .SA_PC_S0(s1_out), .TC_A3(1'b0), .TC_A2(1'b0),
    .TC_A1(1'b0), .TC_Ci(1'b0), .SA_TC_A0(and_1_out), .TC_B3(main_3_tc_b0[3]), .TC_B2(main_3_tc_b0[2]),
    .TC_B1(main_3_tc_b0[1]), .TC_B0(main_3_tc_b0[0]), .PC_B3(main_3_pc_b3), .PC_B2(main_3_pc_b2),
    .PC_B1(main_3_pc_b1), .PC_B0(main_3_pc_b0));  // open: PC_Co, TC_Co, PC_Bo
  LED led_2 (.in(or_2_out));
  or or_2 (or_2_out, main_2_vi, Alarm, main_1_stop);
  not not_2 (not_2_out, ES1_o);
  not not_3 (not_3_out, ES3_o);
  Hex_Digit_Display hex_digit_display_1 (.value(main_3_tc_b0));  // open: dp
  Button Enter_2 (.out(Enter_2_out));
  and and_2 (and_2_out, ES4_o, not_3_out, xnor_1_out);
  or or_3 (or_3_out, Clear_2, Alarm_2);
  Button START_2 (.out(START_2_out));
  Clock Clock_2 (.out(Clock_2_out));
  not not_4 (not_4_out, ES4_o);
  not not_5 (not_5_out, ES2_o);
  not not_6 (not_6_out, ES1_o);
  not not_7 (not_7_out, P1_prime);
  not not_8 (not_8_out, P0_prime);
  and and_3 (and_3_out, ES4_o, not_3_out, not_1_out, not_2_out);
  LED led_3 (.in(Alarm_2));
  Time_Counter_main main_4 (.START(START_2_out), .Enable(Enable_6), .Clock(Clock_2_out), .STOP(main_4_stop));
  not not_9 (not_9_out, E1_prime);
  not not_10 (not_10_out, E0_prime);
  Seat_Allocator_main main_5 (
    .TC_Button(Enter_2_out), .TC_Enable(Enable_2), .TC_Clear(Clear_2), .PC_Button(Enter_2_out),
    .PC_Enable(Enable_2), .PC_Clear(or_3_out), .PC_A3(1'b0), .PC_S3(1'b0), .PC_A2(1'b0), .PC_S2(1'b0),
    .PC_A1(1'b0), .PC_S1(1'b0), .PC_Ci(1'b0), .Bi(1'b0), .SA_PC_A0(and_3_out), .SA_PC_S0(s2_out),
    .TC_A3(1'b0), .TC_A2(1'b0), .TC_A1(1'b0), .TC_Ci(1'b0), .SA_TC_A0(and_2_out), .TC_B3(main_5_tc_b0[3]),
    .TC_B2(main_5_tc_b0[2]), .TC_B1(main_5_tc_b0[1]), .TC_B0(main_5_tc_b0[0]), .PC_B3(main_5_pc_b3),
    .PC_B2(main_5_pc_b2), .PC_B1(main_5_pc_b1), .PC_B0(main_5_pc_b0));  // open: PC_Co, TC_Co, PC_Bo
  Vacancy_Indicator_main main_6 (
    .P1(ES1_o), .P0(ES2_o), .A3(main_5_pc_b3), .A2(main_5_pc_b2), .A1(main_5_pc_b1), .A0(main_5_pc_b0),
    .M3(Max_Capacity_2), .M2(in_25), .M1(in_29), .M0(in_33), .VI(main_6_vi));  // open: Seat_Allotment__SA
  LED led_4 (.in(or_4_out));
  or or_4 (or_4_out, main_6_vi, Alarm_2, main_4_stop);
  and A (A_out, not_7_out, Switch, not_8_out);
  and s1 (s1_out, A_out, not_9_out, not_10_out);
  and s2 (s2_out, A_out, not_9_out, E0_prime);
  and s3 (s3_out, A_out, not_10_out, E1_prime);
  and s4 (s4_out, A_out, E0_prime, E1_prime);
  not not_11 (not_11_out, ES2_o);
  not not_12 (not_12_out, ES1_o);
  Button Enter_3 (.out(Enter_3_out));
  Hex_Digit_Display hex_digit_display_2 (.value(main_5_tc_b0));  // open: dp
  and and_4 (and_4_out, not_4_out, ES3_o, xnor_1_out);
  or or_5 (or_5_out, Clear_3, Alarm_3);
  Button START_3 (.out(START_3_out));
  Clock Clock_3 (.out(Clock_3_out));
  and and_5 (and_5_out, not_4_out, ES3_o, not_5_out, not_6_out);
  LED led_5 (.in(Alarm_3));
  Time_Counter_main main_7 (.START(START_3_out), .Enable(Enable_7), .Clock(Clock_3_out), .STOP(main_7_stop));
  Seat_Allocator_main main_8 (
    .TC_Button(Enter_3_out), .TC_Enable(Enable_3), .TC_Clear(Clear_3), .PC_Button(Enter_3_out),
    .PC_Enable(Enable_3), .PC_Clear(or_5_out), .PC_A3(1'b0), .PC_S3(1'b0), .PC_A2(1'b0), .PC_S2(1'b0),
    .PC_A1(1'b0), .PC_S1(1'b0), .PC_Ci(1'b0), .Bi(1'b0), .SA_PC_A0(and_5_out), .SA_PC_S0(s3_out),
    .TC_A3(1'b0), .TC_A2(1'b0), .TC_A1(1'b0), .TC_Ci(1'b0), .SA_TC_A0(and_4_out), .TC_B3(main_8_tc_b0[3]),
    .TC_B2(main_8_tc_b0[2]), .TC_B1(main_8_tc_b0[1]), .TC_B0(main_8_tc_b0[0]), .PC_B3(main_8_pc_b3),
    .PC_B2(main_8_pc_b2), .PC_B1(main_8_pc_b1), .PC_B0(main_8_pc_b0));  // open: PC_Co, TC_Co, PC_Bo
  Vacancy_Indicator_main main_9 (
    .P1(ES1_o), .P0(ES2_o), .A3(main_8_pc_b3), .A2(main_8_pc_b2), .A1(main_8_pc_b1), .A0(main_8_pc_b0),
    .M3(Max_Capacity_3), .M2(in_26), .M1(in_30), .M0(in_34), .VI(main_9_vi));  // open: Seat_Allotment__SA
  LED led_6 (.in(or_6_out));
  or or_6 (or_6_out, main_9_vi, Alarm_3, main_7_stop);
  Hex_Digit_Display hex_digit_display_3 (.value(main_8_tc_b0));  // open: dp
  Button Enter_4 (.out(Enter_4_out));
  and and_6 (and_6_out, ES4_o, ES3_o, xnor_1_out);
  or or_7 (or_7_out, Clear_4, Alarm_4);
  Button START_4 (.out(START_4_out));
  Clock Clock_4 (.out(Clock_4_out));
  and and_7 (and_7_out, ES4_o, ES3_o, not_11_out, not_12_out);
  LED led_7 (.in(Alarm_4));
  Time_Counter_main main_10 (.START(START_4_out), .Enable(Enable_8), .Clock(Clock_4_out), .STOP(main_10_stop));
  Seat_Allocator_main main_11 (
    .TC_Button(Enter_4_out), .TC_Enable(Enable_4), .TC_Clear(Clear_4), .PC_Button(Enter_4_out),
    .PC_Enable(Enable_4), .PC_Clear(or_7_out), .PC_A3(1'b0), .PC_S3(1'b0), .PC_A2(1'b0), .PC_S2(1'b0),
    .PC_A1(1'b0), .PC_S1(1'b0), .PC_Ci(1'b0), .Bi(1'b0), .SA_PC_A0(and_7_out), .SA_PC_S0(s4_out),
    .TC_A3(1'b0), .TC_A2(1'b0), .TC_A1(1'b0), .TC_Ci(1'b0), .SA_TC_A0(and_6_out), .TC_B3(main_11_tc_b0[3]),
    .TC_B2(main_11_tc_b0[2]), .TC_B1(main_11_tc_b0[1]), .TC_B0(main_11_tc_b0[0]), .PC_B3(main_11_pc_b3),
    .PC_B2(main_11_pc_b2), .PC_B1(main_11_pc_b1), .PC_B0(main_11_pc_b0));  // open: PC_Co, TC_Co, PC_Bo
  Vacancy_Indicator_main main_12 (
    .P1(ES1_o), .P0(ES2_o), .A3(main_11_pc_b3), .A2(main_11_pc_b2), .A1(main_11_pc_b1), .A0(main_11_pc_b0),
    .M3(Max_Capacity_4), .M2(in_27), .M1(in_31), .M0(in_35), .VI(main_12_vi));  // open: Seat_Allotment__SA
  or or_8 (or_8_out, main_12_vi, Alarm_4, main_10_stop);
  LED led_8 (.in(or_8_out));
  Hex_Digit_Display hex_digit_display_4 (.value(main_11_tc_b0));  // open: dp

  // Notes on the sheet:
  //   Emergency Alarm
  //   P1F
  //   P0F
  //   E1F
  //   E0F
  //   Vacancy Indicator
  //   EA_LED
  //   EAI
  //   Time Counter
  //   Event Switcher
  //   PC1
  //   S1
  //   Event-1
  //   Seat Allocator
  //   VI
  //   TCI
  //   Main Person
  //   Type
  //   TC1
  //   LED
  //   Participant Count
  //   Switch Person
  //   Type
  //   Switching Details 
  //   New Event
  //   Type
  //   Old Event
  //   Type
  //   Emergency Alarm
  //   Main Event
  //   Type
  //   PC2
  //   Vacancy Indicator
  //   EA_LED
  //   Time Counter
  //   S2
  //   Event-2
  //   Seat Allocator
  //   VI
  //   EAI
  //   TCI
  //   TC2
  //   LED
  //   w
  //   S1
  //   S2
  //   S3
  //   S4
  //   Participant Count
  //   Vacancy Indicator
  //   Emergency Alarm
  //   PC3
  //   Event-3
  //   Seat Allocator
  //   EA_LED
  //   EAI
  //   TCI
  //   Time Counter
  //   S3
  //   TC3
  //   VI
  //   State Machine For Live Event Navigator
  //   LED
  //   Participant Count
  //   Emergency Alarm
  //   Vacancy Indicator
  //   EA_LED
  //   Time Counter
  //   S4
  //   PC4
  //   Event-4
  //   Seat Allocator
  //   VI
  //   EAI
  //   TCI
  //   TC4
  //   LED
  //   Participant Count
  //   Instructions : 
  //   Team ID : S2-T13 
  //   2 . D. Sai Chaitanya, 231CS220
  //   1 . Bade V N R Mahi Tejesh Reddy, 231CS216 
  //   3 . Lava Kumar Tentu , 231CS230
  //   2. Assign max. capacity to each event.
  //   1. Set the button 'Enable' of each event and time counter to 1. 
  //   4. Give the "Main Person" and "Main Event" type input. 
  //   5. Click on the "Enter" button of respective event to enter into it.
  //   3. Click on the button "START" of Time Counter and set Clock to Tick Enabled.
  //   6. The total "Participant Count" will be displayed on Hex Digit Display. 
  //   7. Give the corresponding switching details if you want to switch the event.
endmodule
